// Logisim project 1.circ as structural Verilog
module bcdssd (
  input  s3,
  input  s2,
  input  s1,
  input  s0,
  output a,
  output b,
  output c,
  output d,
  output e,
  output f,
  output g
);

  wire and_1_out, and_2_out, and_3_out, and_4_out, and_5_out, and_6_out, and_7_out, and_8_out, and_9_out,
       and_10_out, and_11_out, and_12_out, and_13_out, and_14_out, and_15_out, and_16_out, not_1_out,
       not_2_out, not_3_out, not_4_out, not_5_out, not_6_out, not_7_out, not_8_out, not_9_out, not_10_out,
       not_11_out, not_12_out, not_13_out, not_14_out, not_15_out, not_16_out, not_17_out, not_18_out,
       not_19_out, not_20_out, not_21_out;

  not not_1 (not_1_out, s2);
  and and_1 (and_1_out, not_1_out, not_2_out);
  not not_2 (not_2_out, s0);
  and and_2 (and_2_out, s2, s0);
  not not_3 (not_3_out, s2);
  not not_4 (not_4_out, s1);
  and and_3 (and_3_out, not_4_out, not_5_out);
  not not_5 (not_5_out, s0);
  and and_4 (and_4_out, s1, s0);
  not not_6 (not_6_out, s1);
  or or_1 (c, not_6_out, s0, s2);
  not not_7 (not_7_out, s2);
  and and_5 (and_5_out, not_7_out, not_8_out);
  not not_8 (not_8_out, s0);
  not not_9 (not_9_out, s2);
  and and_6 (and_6_out, not_9_out, s1);
  and and_7 (and_7_out, s1, not_10_out);
  not not_10 (not_10_out, s0);
  and and_8 (and_8_out, s2, not_11_out, s0);
  not not_11 (not_11_out, s1);
  not not_12 (not_12_out, s2);
  and and_9 (and_9_out, not_12_out, not_13_out);
  not not_13 (not_13_out, s0);
  and and_10 (and_10_out, s1, not_14_out);
  not not_14 (not_14_out, s0);
  not not_15 (not_15_out, s1);
  and and_11 (and_11_out, not_15_out, not_16_out);
  not not_16 (not_16_out, s0);
  and and_12 (and_12_out, s2, not_17_out);
  not not_17 (not_17_out, s1);
  and and_13 (and_13_out, s2, not_18_out);
  not not_18 (not_18_out, s0);
  not not_19 (not_19_out, s2);
  and and_14 (and_14_out, not_19_out, s1);
  and and_15 (and_15_out, s2, not_20_out);
  not not_20 (not_20_out, s1);
  and and_16 (and_16_out, s2, not_21_out);
  not not_21 (not_21_out, s0);
  or or_2 (a, and_1_out, s1, and_2_out, s3);
  or or_3 (b, not_3_out, and_3_out, and_4_out);
  or or_4 (d, and_5_out, and_6_out, and_7_out, and_8_out, s3);
  or or_5 (e, and_9_out, and_10_out);
  or or_6 (f, and_11_out, and_12_out, and_13_out, s3);
  or or_7 (g, and_14_out, and_15_out, and_16_out, s3);
endmodule

module bcdtest (
  input  [3:0] in_1
);

  wire bcdssd_1_a, bcdssd_1_b, bcdssd_1_c, bcdssd_1_d, bcdssd_1_e, bcdssd_1_f, bcdssd_1_g;

  bcdssd bcdssd_1 (
    .s3(in_1[3]), .s2(in_1[2]), .s1(in_1[1]), .s0(in_1[0]), .a(bcdssd_1_a), .b(bcdssd_1_b), .c(bcdssd_1_c),
    .d(bcdssd_1_d), .e(bcdssd_1_e), .f(bcdssd_1_f), .g(bcdssd_1_g));
  _7_Segment_Display u_7_segment_display_1 (
    .g(bcdssd_1_g), .f(bcdssd_1_f), .a(bcdssd_1_a), .b(bcdssd_1_b), .e(bcdssd_1_e), .d(bcdssd_1_d),
    .c(bcdssd_1_c));  // open: dp
endmodule

module bcddigitadder (
  input  a0,
  input  a1,
  input  a2,
  input  a3,
  input  b0,
  input  b1,
  input  b2,
  input  b3,
  output s3,
  output s2,
  output s1,
  output s0,
  output Cout
);

  wire adder_1_cout, and_1_out, and_2_out;
  wire [3:0] adder_1_out;

  Adder #(.width(4)) adder_1 (
    .a({a3, a2, a1, a0}), .b({b3, b2, b1, b0}), .out(adder_1_out), .cout(adder_1_cout));  // open: cin
  and and_1 (and_1_out, adder_1_out[2], adder_1_out[3]);
  and and_2 (and_2_out, adder_1_out[1], adder_1_out[3]);
  or or_1 (Cout, and_1_out, and_2_out, adder_1_cout);
  Adder #(.width(4)) adder_2 (.a(adder_1_out), .b({1'b0, {2{Cout}}, 1'b0}), .out({s3, s2, s1, s0}));  // open: cin, cout
endmodule
