// Logisim project 345ec164.circ as structural Verilog: 5 circuits, main circuit 3a
module _3a (
);

  wire bcd7sdecoder_1_a, bcd7sdecoder_1_b, bcd7sdecoder_1_c, bcd7sdecoder_1_d, bcd7sdecoder_1_e,
       bcd7sdecoder_1_f, bcd7sdecoder_1_g, Clock_out, JK_FF_2_q, JK_FF_2_qn, JK_FF_3_q, JK_FF_q, JK_FF_qn;

  Clock Clock (.out(Clock_out));
  J_K_Flip_Flop JK_FF (.J(1'b1), .clk(Clock_out), .K(1'b1), .Q(JK_FF_q), .Qn(JK_FF_qn));  // open: preset, en, reset
  J_K_Flip_Flop JK_FF_2 (
    .J(1'b1), .clk(JK_FF_qn), .K(1'b1), .Q(JK_FF_2_q), .Qn(JK_FF_2_qn));  // open: preset, en, reset
  J_K_Flip_Flop JK_FF_3 (.J(1'b1), .clk(JK_FF_2_qn), .K(1'b1), .Q(JK_FF_3_q));  // open: Qn, preset, en, reset
  _7_Segment_Display u_7_segment_display_1 (
    .g(bcd7sdecoder_1_g), .f(bcd7sdecoder_1_f), .a(bcd7sdecoder_1_a), .b(bcd7sdecoder_1_b),
    .e(bcd7sdecoder_1_e), .d(bcd7sdecoder_1_d), .c(bcd7sdecoder_1_c));  // open: dp
  bcd7sdecoder bcd7sdecoder_1 (
    .s0(JK_FF_q), .s1(JK_FF_2_q), .s2(JK_FF_3_q), .s3(1'b0), .a(bcd7sdecoder_1_a), .b(bcd7sdecoder_1_b),
    .c(bcd7sdecoder_1_c), .d(bcd7sdecoder_1_d), .e(bcd7sdecoder_1_e), .f(bcd7sdecoder_1_f),
    .g(bcd7sdecoder_1_g));
endmodule

module _3b (
  input  in_1
);

  wire bcd7sdecoder_1_a, bcd7sdecoder_1_b, bcd7sdecoder_1_c, bcd7sdecoder_1_d, bcd7sdecoder_1_e,
       bcd7sdecoder_1_f, bcd7sdecoder_1_g, clock_1_out;
  wire [2:0] j_k_ff_1_q, j_k_ff_1_qn, multiplexer_1_out;

  Clock clock_1 (.out(clock_1_out));
  J_K_Flip_Flop j_k_ff_1 (
    .J(1'b1), .clk(clock_1_out), .K(1'b1), .Q(j_k_ff_1_q[0]), .Qn(j_k_ff_1_qn[0]));  // open: preset, en, reset
  J_K_Flip_Flop j_k_ff_2 (
    .J(1'b1), .clk(j_k_ff_1_qn[0]), .K(1'b1), .Q(j_k_ff_1_q[1]), .Qn(j_k_ff_1_qn[1]));  // open: preset, en, reset
  J_K_Flip_Flop j_k_ff_3 (
    .J(1'b1), .clk(j_k_ff_1_qn[1]), .K(1'b1), .Q(j_k_ff_1_q[2]), .Qn(j_k_ff_1_qn[2]));  // open: preset, en, reset
  Multiplexer #(.width(3)) multiplexer_1 (
    .in0(j_k_ff_1_q), .in1(j_k_ff_1_qn), .out(multiplexer_1_out), .sel(in_1));  // open: en
  bcd7sdecoder bcd7sdecoder_1 (
    .s0(multiplexer_1_out[0]), .s1(multiplexer_1_out[1]), .s2(multiplexer_1_out[2]), .s3(1'b0),
    .a(bcd7sdecoder_1_a), .b(bcd7sdecoder_1_b), .c(bcd7sdecoder_1_c), .d(bcd7sdecoder_1_d),
    .e(bcd7sdecoder_1_e), .f(bcd7sdecoder_1_f), .g(bcd7sdecoder_1_g));
  _7_Segment_Display u_7_segment_display_1 (
    .g(bcd7sdecoder_1_g), .f(bcd7sdecoder_1_f), .a(bcd7sdecoder_1_a), .b(bcd7sdecoder_1_b),
    .e(bcd7sdecoder_1_e), .d(bcd7sdecoder_1_d), .c(bcd7sdecoder_1_c));  // open: dp
endmodule

module _4 (
  output [3:0] out_1
);

  wire and_1_out, bcd7sdecoder_1_a, bcd7sdecoder_1_b, bcd7sdecoder_1_c, bcd7sdecoder_1_d, bcd7sdecoder_1_e,
       bcd7sdecoder_1_f, bcd7sdecoder_1_g, bcd7sdecoder_2_a, bcd7sdecoder_2_b, bcd7sdecoder_2_c,
       bcd7sdecoder_2_d, bcd7sdecoder_2_e, bcd7sdecoder_2_f, bcd7sdecoder_2_g, clock_1_out, j_k_ff_1_qn,
       j_k_ff_2_qn, j_k_ff_3_qn;

  Clock clock_1 (.out(clock_1_out));
  J_K_Flip_Flop j_k_ff_1 (
    .J(1'b1), .clk(clock_1_out), .K(1'b1), .Q(out_1[0]), .Qn(j_k_ff_1_qn), .reset(and_1_out));  // open: preset, en
  J_K_Flip_Flop j_k_ff_2 (
    .J(1'b1), .clk(j_k_ff_1_qn), .K(1'b1), .Q(out_1[1]), .Qn(j_k_ff_2_qn), .reset(and_1_out));  // open: preset, en
  J_K_Flip_Flop j_k_ff_3 (
    .J(1'b1), .clk(j_k_ff_2_qn), .K(1'b1), .Q(out_1[2]), .Qn(j_k_ff_3_qn), .reset(and_1_out));  // open: preset, en
  J_K_Flip_Flop j_k_ff_4 (
    .J(1'b1), .clk(j_k_ff_3_qn), .K(1'b1), .Q(out_1[3]), .reset(and_1_out));  // open: Qn, preset, en
  and and_1 (and_1_out, out_1[3], j_k_ff_3_qn, out_1[1], out_1[0]);
  _7_Segment_Display u_7_segment_display_1 (
    .g(bcd7sdecoder_1_g), .f(bcd7sdecoder_1_f), .a(bcd7sdecoder_1_a), .b(bcd7sdecoder_1_b),
    .e(bcd7sdecoder_1_e), .d(bcd7sdecoder_1_d), .c(bcd7sdecoder_1_c));  // open: dp
  bcd7sdecoder bcd7sdecoder_1 (
    .s1(1'b0), .s2(1'b0), .s3(1'b0), .a(bcd7sdecoder_1_a), .b(bcd7sdecoder_1_b), .c(bcd7sdecoder_1_c),
    .d(bcd7sdecoder_1_d), .e(bcd7sdecoder_1_e), .f(bcd7sdecoder_1_f), .g(bcd7sdecoder_1_g));  // open: s0
  bcd7sdecoder bcd7sdecoder_2 (
    .s0(out_1[0]), .s1(out_1[1]), .s2(out_1[2]), .s3(1'b0), .a(bcd7sdecoder_2_a), .b(bcd7sdecoder_2_b),
    .c(bcd7sdecoder_2_c), .d(bcd7sdecoder_2_d), .e(bcd7sdecoder_2_e), .f(bcd7sdecoder_2_f),
    .g(bcd7sdecoder_2_g));
  _7_Segment_Display u_7_segment_display_2 (
    .g(bcd7sdecoder_2_g), .f(bcd7sdecoder_2_f), .a(bcd7sdecoder_2_a), .b(bcd7sdecoder_2_b),
    .e(bcd7sdecoder_2_e), .d(bcd7sdecoder_2_d), .c(bcd7sdecoder_2_c));  // open: dp
endmodule

module _5 (
);

  wire and_1_out, BCD_to_7segement_decoder_a, BCD_to_7segement_decoder_b, BCD_to_7segement_decoder_c,
       BCD_to_7segement_decoder_d, BCD_to_7segement_decoder_e, BCD_to_7segement_decoder_f,
       BCD_to_7segement_decoder_g, clock_out, j_k_ff_1_q, j_k_ff_1_qn, j_k_ff_2_q, j_k_ff_2_qn, j_k_ff_3_q;

  Clock clock (.out(clock_out));
  J_K_Flip_Flop j_k_ff_1 (
    .J(1'b1), .clk(clock_out), .K(1'b1), .Q(j_k_ff_1_q), .Qn(j_k_ff_1_qn), .reset(and_1_out));  // open: preset, en
  J_K_Flip_Flop j_k_ff_2 (
    .J(1'b1), .clk(j_k_ff_1_qn), .K(1'b1), .Q(j_k_ff_2_q), .Qn(j_k_ff_2_qn), .reset(and_1_out));  // open: preset, en
  J_K_Flip_Flop j_k_ff_3 (
    .J(1'b1), .clk(j_k_ff_2_qn), .K(1'b1), .Q(j_k_ff_3_q), .reset(and_1_out));  // open: Qn, preset, en
  and and_1 (and_1_out, j_k_ff_3_q, j_k_ff_1_q, j_k_ff_2_q);
  bcd7sdecoder BCD_to_7segement_decoder (
    .s0(j_k_ff_1_q), .s1(j_k_ff_2_q), .s2(j_k_ff_3_q), .s3(1'b0), .a(BCD_to_7segement_decoder_a),
    .b(BCD_to_7segement_decoder_b), .c(BCD_to_7segement_decoder_c), .d(BCD_to_7segement_decoder_d),
    .e(BCD_to_7segement_decoder_e), .f(BCD_to_7segement_decoder_f), .g(BCD_to_7segement_decoder_g));
  _7_Segment_Display u_7_segment_display_1 (
    .g(BCD_to_7segement_decoder_g), .f(BCD_to_7segement_decoder_f), .a(BCD_to_7segement_decoder_a),
    .b(BCD_to_7segement_decoder_b), .e(BCD_to_7segement_decoder_e), .d(BCD_to_7segement_decoder_d),
    .c(BCD_to_7segement_decoder_c));  // open: dp
endmodule

module bcd7sdecoder (
  input  s0,
  input  s1,
  input  s2,
  input  s3,
  output a,
  output b,
  output c,
  output d,
  output e,
  output f,
  output g
);

  wire and_1_out, and_2_out, and_3_out, and_4_out, and_5_out, and_6_out, and_7_out, and_8_out, and_9_out,
       and_10_out, and_11_out, and_12_out, and_13_out, and_14_out, and_15_out, and_16_out, not_1_out,
       not_2_out, not_3_out, not_4_out, not_5_out, not_6_out, not_7_out, not_8_out, not_9_out, not_10_out,
       not_11_out, not_12_out, not_13_out, not_14_out, not_15_out, not_16_out, not_17_out, not_18_out,
       not_19_out, not_20_out, not_21_out;

  not not_1 (not_1_out, s2);
  and and_1 (and_1_out, not_1_out, not_2_out);
  not not_2 (not_2_out, s0);
  and and_2 (and_2_out, s2, s0);
  not not_3 (not_3_out, s0);
  and and_3 (and_3_out, not_3_out, not_4_out);
  not not_4 (not_4_out, s1);
  not not_5 (not_5_out, s2);
  and and_4 (and_4_out, s0, s1);
  not not_6 (not_6_out, s1);
  or or_1 (c, not_6_out, s2, s0);
  not not_7 (not_7_out, s0);
  and and_5 (and_5_out, not_7_out, not_8_out);
  not not_8 (not_8_out, s2);
  not not_9 (not_9_out, s0);
  and and_6 (and_6_out, not_9_out, s1);
  and and_7 (and_7_out, s1, not_10_out);
  not not_10 (not_10_out, s2);
  not not_11 (not_11_out, s1);
  and and_8 (and_8_out, s0, not_11_out, s2);
  not not_12 (not_12_out, s0);
  and and_9 (and_9_out, not_12_out, not_13_out);
  not not_13 (not_13_out, s2);
  not not_14 (not_14_out, s0);
  and and_10 (and_10_out, not_14_out, s1);
  not not_15 (not_15_out, s0);
  and and_11 (and_11_out, not_15_out, not_16_out);
  not not_16 (not_16_out, s1);
  not not_17 (not_17_out, s0);
  and and_12 (and_12_out, not_17_out, s2);
  not not_18 (not_18_out, s1);
  and and_13 (and_13_out, not_18_out, s2);
  not not_19 (not_19_out, s1);
  and and_14 (and_14_out, not_19_out, s2);
  not not_20 (not_20_out, s0);
  and and_15 (and_15_out, not_20_out, s1);
  and and_16 (and_16_out, s1, not_21_out);
  not not_21 (not_21_out, s2);
  or or_2 (a, and_1_out, s1, and_2_out, s3);
  or or_3 (b, and_3_out, not_5_out, and_4_out);
  or or_4 (d, and_5_out, s3, and_6_out, and_7_out, and_8_out);
  or or_5 (e, and_9_out, and_10_out);
  or or_6 (f, and_11_out, s3, and_12_out, and_13_out);
  or or_7 (g, s3, and_14_out, and_15_out, and_16_out);
endmodule
