// Logisim project bkp.circ as structural Verilog
module bcdssd (
  input  s0,
  input  s1,
  input  s2,
  input  s3,
  output a,
  output b,
  output c,
  output d,
  output e,
  output f,
  output g
);

  wire and_1_out, and_2_out, and_3_out, and_4_out, and_5_out, and_6_out, and_7_out, and_8_out, and_9_out,
       and_10_out, and_11_out, and_12_out, and_13_out, and_14_out, and_15_out, and_16_out, not_1_out,
       not_2_out, not_3_out, not_4_out, not_5_out, not_6_out, not_7_out, not_8_out, not_9_out, not_10_out,
       not_11_out, not_12_out, not_13_out, not_14_out, not_15_out, not_16_out, not_17_out, not_18_out,
       not_19_out, not_20_out, not_21_out;

  not not_1 (not_1_out, s2);
  and and_1 (and_1_out, not_1_out, not_2_out);
  not not_2 (not_2_out, s0);
  and and_2 (and_2_out, s2, s0);
  not not_3 (not_3_out, s2);
  not not_4 (not_4_out, s1);
  and and_3 (and_3_out, not_4_out, not_5_out);
  not not_5 (not_5_out, s0);
  and and_4 (and_4_out, s1, s0);
  not not_6 (not_6_out, s1);
  or or_1 (c, not_6_out, s0, s2);
  not not_7 (not_7_out, s2);
  and and_5 (and_5_out, not_7_out, not_8_out);
  not not_8 (not_8_out, s0);
  not not_9 (not_9_out, s2);
  and and_6 (and_6_out, not_9_out, s1);
  and and_7 (and_7_out, s1, not_10_out);
  not not_10 (not_10_out, s0);
  not not_11 (not_11_out, s1);
  and and_8 (and_8_out, s2, not_11_out, s0);
  not not_12 (not_12_out, s2);
  and and_9 (and_9_out, not_12_out, not_13_out);
  not not_13 (not_13_out, s0);
  and and_10 (and_10_out, s1, not_14_out);
  not not_14 (not_14_out, s0);
  not not_15 (not_15_out, s1);
  and and_11 (and_11_out, not_15_out, not_16_out);
  not not_16 (not_16_out, s0);
  and and_12 (and_12_out, s2, not_17_out);
  not not_17 (not_17_out, s1);
  and and_13 (and_13_out, s2, not_18_out);
  not not_18 (not_18_out, s0);
  not not_19 (not_19_out, s2);
  and and_14 (and_14_out, not_19_out, s1);
  and and_15 (and_15_out, s2, not_20_out);
  not not_20 (not_20_out, s1);
  and and_16 (and_16_out, s2, not_21_out);
  not not_21 (not_21_out, s0);
  or or_2 (a, and_1_out, s1, and_2_out, s3);
  or or_3 (b, not_3_out, and_3_out, and_4_out);
  or or_4 (d, and_5_out, and_6_out, and_7_out, and_8_out, s3);
  or or_5 (e, and_9_out, and_10_out);
  or or_6 (f, and_11_out, and_12_out, and_13_out, s3);
  or or_7 (g, and_14_out, and_15_out, and_16_out, s3);
endmodule

module bcdtest (
  input  [3:0] in_1
);

  wire bcdssd_1_a, bcdssd_1_b, bcdssd_1_c, bcdssd_1_d, bcdssd_1_e, bcdssd_1_f, bcdssd_1_g;

  bcdssd bcdssd_1 (
    .s0(in_1[0]), .s1(in_1[1]), .s2(in_1[2]), .s3(in_1[3]), .a(bcdssd_1_a), .b(bcdssd_1_b), .c(bcdssd_1_c),
    .d(bcdssd_1_d), .e(bcdssd_1_e), .f(bcdssd_1_f), .g(bcdssd_1_g));
  _7_Segment_Display u_7_segment_display_1 (
    .g(bcdssd_1_g), .f(bcdssd_1_f), .a(bcdssd_1_a), .b(bcdssd_1_b), .e(bcdssd_1_e), .d(bcdssd_1_d),
    .c(bcdssd_1_c));  // open: dp
endmodule

module bcddigitadder (
  input  Cin,
  input  a0,
  input  a1,
  input  a2,
  input  a3,
  input  b0,
  input  b1,
  input  b2,
  input  b3,
  output s0,
  output s1,
  output s2,
  output s3,
  output Cout
);

  wire adder_1_cout, and_1_out, and_2_out;
  wire [3:0] adder_1_out;

  Adder #(.width(4)) adder_1 (
    .a({a3, a2, a1, a0}), .b({b3, b2, b1, b0}), .out(adder_1_out), .cin(Cin), .cout(adder_1_cout));
  and and_1 (and_1_out, adder_1_out[2], adder_1_out[3]);
  and and_2 (and_2_out, adder_1_out[1], adder_1_out[3]);
  or or_1 (Cout, and_1_out, and_2_out, adder_1_cout);
  Adder #(.width(4)) adder_2 (.a(adder_1_out), .b({1'b0, {2{Cout}}, 1'b0}), .out({s3, s2, s1, s0}));  // open: cin, cout
endmodule

module bcd2digitadder (
  input  a0,
  input  a1,
  input  a2,
  input  a3,
  input  a4,
  input  a5,
  input  a6,
  input  a7,
  input  b0,
  input  b1,
  input  b2,
  input  b3,
  input  b4,
  input  b5,
  input  b6,
  input  b7,
  output s0,
  output s1,
  output s2,
  output s3,
  output s4,
  output s5,
  output s6,
  output s7,
  output Cout
);

  wire BCD_Single_Digit_Adder_cout;

  bcddigitadder BCD_Single_Digit_Adder (
    .a0(a0), .a1(a1), .a2(a2), .a3(a3), .b0(b0), .b1(b1), .b2(b2), .b3(b3), .s0(s0), .s1(s1), .s2(s2),
    .s3(s3), .Cout(BCD_Single_Digit_Adder_cout));  // open: Cin
  bcddigitadder BCD_Single_Digit_Adder_2 (
    .Cin(BCD_Single_Digit_Adder_cout), .a0(a4), .a1(a5), .a2(a6), .a3(a7), .b0(b4), .b1(b5), .b2(b6),
    .b3(b7), .s0(s4), .s1(s5), .s2(s6), .s3(s7), .Cout(Cout));

  // Notes on the sheet:
  //   201ec164
endmodule

module bcd2digitadderdisplay (
  input  [7:0] A,
  input  [7:0] B
);

  wire bcd2digitadder_1_cout, bcd2digitadder_1_s0, bcd2digitadder_1_s1, bcd2digitadder_1_s2,
       bcd2digitadder_1_s3, bcd2digitadder_1_s4, bcd2digitadder_1_s5, bcd2digitadder_1_s6,
       bcd2digitadder_1_s7, bcdssd_1_a, bcdssd_1_b, bcdssd_1_c, bcdssd_1_d, bcdssd_1_e, bcdssd_1_f,
       bcdssd_1_g, bcdssd_2_a, bcdssd_2_b, bcdssd_2_c, bcdssd_2_d, bcdssd_2_e, bcdssd_2_f, bcdssd_2_g,
       bcdssd_3_a, bcdssd_3_b, bcdssd_3_c, bcdssd_3_d, bcdssd_3_e, bcdssd_3_f, bcdssd_3_g;

  bcd2digitadder bcd2digitadder_1 (
    .a0(A[0]), .a1(A[1]), .a2(A[2]), .a3(A[3]), .a4(A[4]), .a5(A[5]), .a6(A[6]), .a7(A[7]), .b0(B[0]),
    .b1(B[1]), .b2(B[2]), .b3(B[3]), .b4(B[4]), .b5(B[5]), .b6(B[6]), .b7(B[7]), .s0(bcd2digitadder_1_s0),
    .s1(bcd2digitadder_1_s1), .s2(bcd2digitadder_1_s2), .s3(bcd2digitadder_1_s3), .s4(bcd2digitadder_1_s4),
    .s5(bcd2digitadder_1_s5), .s6(bcd2digitadder_1_s6), .s7(bcd2digitadder_1_s7), .Cout(bcd2digitadder_1_cout));
  bcdssd bcdssd_1 (
    .s0(bcd2digitadder_1_s0), .s1(bcd2digitadder_1_s1), .s2(bcd2digitadder_1_s2), .s3(bcd2digitadder_1_s3),
    .a(bcdssd_1_a), .b(bcdssd_1_b), .c(bcdssd_1_c), .d(bcdssd_1_d), .e(bcdssd_1_e), .f(bcdssd_1_f),
    .g(bcdssd_1_g));
  bcdssd bcdssd_2 (
    .s0(bcd2digitadder_1_cout), .s1(1'b0), .s2(1'b0), .s3(1'b0), .a(bcdssd_2_a), .b(bcdssd_2_b),
    .c(bcdssd_2_c), .d(bcdssd_2_d), .e(bcdssd_2_e), .f(bcdssd_2_f), .g(bcdssd_2_g));
  bcdssd bcdssd_3 (
    .s0(bcd2digitadder_1_s4), .s1(bcd2digitadder_1_s5), .s2(bcd2digitadder_1_s6), .s3(bcd2digitadder_1_s7),
    .a(bcdssd_3_a), .b(bcdssd_3_b), .c(bcdssd_3_c), .d(bcdssd_3_d), .e(bcdssd_3_e), .f(bcdssd_3_f),
    .g(bcdssd_3_g));
  _7_Segment_Display u_7_segment_display_1 (
    .g(bcdssd_2_g), .f(bcdssd_2_f), .a(bcdssd_2_a), .b(bcdssd_2_b), .e(bcdssd_2_e), .d(bcdssd_2_d),
    .c(bcdssd_2_c));  // open: dp
  _7_Segment_Display u_7_segment_display_2 (
    .g(bcdssd_3_g), .f(bcdssd_3_f), .a(bcdssd_3_a), .b(bcdssd_3_b), .e(bcdssd_3_e), .d(bcdssd_3_d),
    .c(bcdssd_3_c));  // open: dp
  _7_Segment_Display u_7_segment_display_3 (
    .g(bcdssd_1_g), .f(bcdssd_1_f), .a(bcdssd_1_a), .b(bcdssd_1_b), .e(bcdssd_1_e), .d(bcdssd_1_d),
    .c(bcdssd_1_c));  // open: dp
endmodule

module bcddigitadderdisplay (
  input  [3:0] A,
  input  [3:0] B
);

  wire bcddigitadder_1_cout, bcddigitadder_1_s0, bcddigitadder_1_s1, bcddigitadder_1_s2, bcddigitadder_1_s3,
       bcdssd_1_a, bcdssd_1_b, bcdssd_1_c, bcdssd_1_d, bcdssd_1_e, bcdssd_1_f, bcdssd_1_g, bcdssd_2_a,
       bcdssd_2_b, bcdssd_2_c, bcdssd_2_d, bcdssd_2_e, bcdssd_2_f, bcdssd_2_g;

  bcddigitadder bcddigitadder_1 (
    .Cin(1'b0), .a0(A[0]), .a1(A[1]), .a2(A[2]), .a3(A[3]), .b0(B[0]), .b1(B[1]), .b2(B[2]), .b3(B[3]),
    .s0(bcddigitadder_1_s0), .s1(bcddigitadder_1_s1), .s2(bcddigitadder_1_s2), .s3(bcddigitadder_1_s3),
    .Cout(bcddigitadder_1_cout));
  bcdssd bcdssd_1 (
    .s0(bcddigitadder_1_s0), .s1(bcddigitadder_1_s1), .s2(bcddigitadder_1_s2), .s3(bcddigitadder_1_s3),
    .a(bcdssd_1_a), .b(bcdssd_1_b), .c(bcdssd_1_c), .d(bcdssd_1_d), .e(bcdssd_1_e), .f(bcdssd_1_f),
    .g(bcdssd_1_g));
  bcdssd bcdssd_2 (
    .s0(bcddigitadder_1_cout), .s1(1'b0), .s2(1'b0), .s3(1'b0), .a(bcdssd_2_a), .b(bcdssd_2_b),
    .c(bcdssd_2_c), .d(bcdssd_2_d), .e(bcdssd_2_e), .f(bcdssd_2_f), .g(bcdssd_2_g));
  _7_Segment_Display u_7_segment_display_1 (
    .g(bcdssd_2_g), .f(bcdssd_2_f), .a(bcdssd_2_a), .b(bcdssd_2_b), .e(bcdssd_2_e), .d(bcdssd_2_d),
    .c(bcdssd_2_c));  // open: dp
  _7_Segment_Display u_7_segment_display_2 (
    .g(bcdssd_1_g), .f(bcdssd_1_f), .a(bcdssd_1_a), .b(bcdssd_1_b), .e(bcdssd_1_e), .d(bcdssd_1_d),
    .c(bcdssd_1_c));  // open: dp
endmodule
