// Logisim project q1toq3.circ as structural Verilog: 4 circuits, main circuit q1_201ec164
module q1_201ec164 (
);

  wire and_1_out, and_2_out, and_3_out, bcd_to_7_segment_decoder_1_p1, bcd_to_7_segment_decoder_1_p2,
       bcd_to_7_segment_decoder_1_p3, bcd_to_7_segment_decoder_1_p4, bcd_to_7_segment_decoder_1_p6,
       bcd_to_7_segment_decoder_1_p7, bcd_to_7_segment_decoder_1_p8, binary_to_bcd_converter_1_p2,
       clock_1_out, d_ff_1_qn, d_ff_3_qn, xor_1_out;
  wire [2:0] binary_to_bcd_converter_1_p1;

  Clock clock_1 (.out(clock_1_out));
  and and_1 (and_1_out, binary_to_bcd_converter_1_p1[0], binary_to_bcd_converter_1_p1[1], d_ff_1_qn);
  D_Flip_Flop d_ff_1 (
    .D(and_1_out), .clk(clock_1_out), .Q(binary_to_bcd_converter_1_p1[2]), .Qn(d_ff_1_qn));  // open: preset, reset
  xor xor_1 (xor_1_out, binary_to_bcd_converter_1_p1[0], binary_to_bcd_converter_1_p1[1]);
  and and_2 (and_2_out, d_ff_1_qn, xor_1_out);
  D_Flip_Flop d_ff_2 (
    .D(and_2_out), .clk(clock_1_out), .Q(binary_to_bcd_converter_1_p1[1]));  // open: Qn, preset, reset
  and and_3 (and_3_out, d_ff_1_qn, d_ff_3_qn);
  // Binary_to_BCD_converter #(.binvalue(4)) binary_to_bcd_converter_1: pin names not known; wires that end beside it: {1'b0, binary_to_bcd_converter_1_p1}, binary_to_bcd_converter_1_p2
  D_Flip_Flop d_ff_3 (
    .D(and_3_out), .clk(clock_1_out), .Q(binary_to_bcd_converter_1_p1[0]), .Qn(d_ff_3_qn));  // open: preset, reset
  // BCD_to_7_Segment_decoder bcd_to_7_segment_decoder_1: pin names not known; wires that end beside it: bcd_to_7_segment_decoder_1_p1, bcd_to_7_segment_decoder_1_p2, bcd_to_7_segment_decoder_1_p3, bcd_to_7_segment_decoder_1_p4, binary_to_bcd_converter_1_p2, bcd_to_7_segment_decoder_1_p6, bcd_to_7_segment_decoder_1_p7, bcd_to_7_segment_decoder_1_p8
  _7_Segment_Display u_7_segment_display_1 (
    .g(bcd_to_7_segment_decoder_1_p1), .f(bcd_to_7_segment_decoder_1_p3), .a(bcd_to_7_segment_decoder_1_p6),
    .b(bcd_to_7_segment_decoder_1_p8), .e(bcd_to_7_segment_decoder_1_p2), .d(bcd_to_7_segment_decoder_1_p4),
    .c(bcd_to_7_segment_decoder_1_p7));  // open: dp
endmodule

module q2_201ec164 (
  input  S,
  output [3:0] out_2
);

  wire and_1_out, and_2_out, and_3_out, and_4_out, and_5_out, and_6_out, bcd_to_7_segment_decoder_1_p1,
       bcd_to_7_segment_decoder_1_p2, bcd_to_7_segment_decoder_1_p3, bcd_to_7_segment_decoder_1_p4,
       bcd_to_7_segment_decoder_1_p6, bcd_to_7_segment_decoder_1_p7, bcd_to_7_segment_decoder_1_p8,
       bcd_to_7_segment_decoder_2_p1, bcd_to_7_segment_decoder_2_p2, bcd_to_7_segment_decoder_2_p3,
       bcd_to_7_segment_decoder_2_p4, bcd_to_7_segment_decoder_2_p6, bcd_to_7_segment_decoder_2_p7,
       bcd_to_7_segment_decoder_2_p8, binary_to_bcd_converter_1_p2, binary_to_bcd_converter_1_p3,
       clock_1_out, j_k_ff_1_qn, j_k_ff_2_qn, j_k_ff_3_qn, not_1_out, or_1_out, or_2_out, or_3_out;

  Clock clock_1 (.out(clock_1_out));
  not not_1 (not_1_out, S);
  J_K_Flip_Flop j_k_ff_1 (
    .J(1'b1), .K(1'b1), .clk(clock_1_out), .Q(out_2[0]), .Qn(j_k_ff_1_qn));  // open: preset, reset
  and and_1 (and_1_out, not_1_out, out_2[0]);
  and and_2 (and_2_out, S, j_k_ff_1_qn);
  J_K_Flip_Flop j_k_ff_2 (
    .J(or_1_out), .K(or_1_out), .clk(clock_1_out), .Q(out_2[1]), .Qn(j_k_ff_2_qn));  // open: preset, reset
  or or_1 (or_1_out, and_1_out, and_2_out);
  and and_3 (and_3_out, and_1_out, out_2[1]);
  or or_2 (or_2_out, and_3_out, and_4_out);
  and and_4 (and_4_out, j_k_ff_2_qn, and_2_out);
  J_K_Flip_Flop j_k_ff_3 (
    .J(or_2_out), .K(or_2_out), .clk(clock_1_out), .Q(out_2[2]), .Qn(j_k_ff_3_qn));  // open: preset, reset
  // Binary_to_BCD_converter #(.binvalue(4)) binary_to_bcd_converter_1: pin names not known; wires that end beside it: out_2, binary_to_bcd_converter_1_p2, binary_to_bcd_converter_1_p3
  and and_5 (and_5_out, and_3_out, out_2[2]);
  and and_6 (and_6_out, j_k_ff_3_qn, and_4_out);
  // BCD_to_7_Segment_decoder bcd_to_7_segment_decoder_1: pin names not known; wires that end beside it: bcd_to_7_segment_decoder_1_p1, bcd_to_7_segment_decoder_1_p2, bcd_to_7_segment_decoder_1_p3, bcd_to_7_segment_decoder_1_p4, binary_to_bcd_converter_1_p2, bcd_to_7_segment_decoder_1_p6, bcd_to_7_segment_decoder_1_p7, bcd_to_7_segment_decoder_1_p8
  J_K_Flip_Flop j_k_ff_4 (.J(or_3_out), .K(or_3_out), .clk(clock_1_out), .Q(out_2[3]));  // open: Qn, preset, reset
  or or_3 (or_3_out, and_5_out, and_6_out);
  _7_Segment_Display u_7_segment_display_1 (
    .g(bcd_to_7_segment_decoder_1_p1), .f(bcd_to_7_segment_decoder_1_p3), .a(bcd_to_7_segment_decoder_1_p6),
    .b(bcd_to_7_segment_decoder_1_p8), .e(bcd_to_7_segment_decoder_1_p2), .d(bcd_to_7_segment_decoder_1_p4),
    .c(bcd_to_7_segment_decoder_1_p7));  // open: dp
  // BCD_to_7_Segment_decoder bcd_to_7_segment_decoder_2: pin names not known; wires that end beside it: bcd_to_7_segment_decoder_2_p1, bcd_to_7_segment_decoder_2_p2, bcd_to_7_segment_decoder_2_p3, bcd_to_7_segment_decoder_2_p4, binary_to_bcd_converter_1_p3, bcd_to_7_segment_decoder_2_p6, bcd_to_7_segment_decoder_2_p7, bcd_to_7_segment_decoder_2_p8
  _7_Segment_Display u_7_segment_display_2 (
    .g(bcd_to_7_segment_decoder_2_p1), .f(bcd_to_7_segment_decoder_2_p3), .a(bcd_to_7_segment_decoder_2_p6),
    .b(bcd_to_7_segment_decoder_2_p8), .e(bcd_to_7_segment_decoder_2_p2), .d(bcd_to_7_segment_decoder_2_p4),
    .c(bcd_to_7_segment_decoder_2_p7));  // open: dp

  // Notes on the sheet:
  //   s:0 up counter / s:1 down counter
endmodule

module q3_201ec164 (
  output [3:0] out_1
);

  wire and_1_out, and_2_out, and_3_out, and_4_out, and_5_out, and_6_out, and_7_out, and_8_out, and_9_out,
       and_10_out, and_11_out, and_12_out, bcd_to_7_segment_decoder_1_p1, bcd_to_7_segment_decoder_1_p2,
       bcd_to_7_segment_decoder_1_p3, bcd_to_7_segment_decoder_1_p4, bcd_to_7_segment_decoder_1_p6,
       bcd_to_7_segment_decoder_1_p7, bcd_to_7_segment_decoder_1_p8, bcd_to_7_segment_decoder_2_p1,
       bcd_to_7_segment_decoder_2_p2, bcd_to_7_segment_decoder_2_p3, bcd_to_7_segment_decoder_2_p4,
       bcd_to_7_segment_decoder_2_p6, bcd_to_7_segment_decoder_2_p7, bcd_to_7_segment_decoder_2_p8,
       binary_to_bcd_converter_1_p2, binary_to_bcd_converter_1_p3, clock_1_out, d_ff_1_qn, d_ff_2_qn,
       d_ff_3_qn, d_ff_4_qn, or_1_out, or_2_out, or_3_out, or_4_out;

  or or_1 (or_1_out, and_1_out, and_2_out, and_3_out);
  Clock clock_1 (.out(clock_1_out));
  and and_1 (and_1_out, out_1[0], d_ff_3_qn, out_1[2], out_1[3]);
  and and_2 (and_2_out, d_ff_4_qn, out_1[1], out_1[2], d_ff_1_qn);
  and and_3 (and_3_out, d_ff_4_qn, d_ff_3_qn, d_ff_2_qn);
  D_Flip_Flop d_ff_1 (.D(or_1_out), .clk(clock_1_out), .Q(out_1[3]), .Qn(d_ff_1_qn));  // open: preset, reset
  and and_4 (and_4_out, out_1[3], d_ff_4_qn, d_ff_3_qn);
  D_Flip_Flop d_ff_2 (.D(or_2_out), .clk(clock_1_out), .Q(out_1[2]), .Qn(d_ff_2_qn));  // open: preset, reset
  or or_2 (or_2_out, and_4_out, and_5_out, and_6_out);
  and and_5 (and_5_out, out_1[3], d_ff_2_qn, out_1[1], out_1[0]);
  and and_6 (and_6_out, d_ff_1_qn, out_1[2], out_1[1], d_ff_4_qn);
  and and_7 (and_7_out, out_1[3], out_1[2], d_ff_3_qn);
  or or_3 (or_3_out, and_7_out, and_8_out, and_9_out);
  and and_8 (and_8_out, d_ff_1_qn, out_1[2], out_1[0], out_1[1]);
  D_Flip_Flop d_ff_3 (.D(or_3_out), .clk(clock_1_out), .Q(out_1[1]), .Qn(d_ff_3_qn));  // open: preset, reset
  and and_9 (and_9_out, out_1[3], d_ff_2_qn, out_1[1], out_1[0]);
  // Binary_to_BCD_converter #(.binvalue(4)) binary_to_bcd_converter_1: pin names not known; wires that end beside it: out_1, binary_to_bcd_converter_1_p2, binary_to_bcd_converter_1_p3
  or or_4 (or_4_out, and_10_out, and_11_out, and_12_out);
  // BCD_to_7_Segment_decoder bcd_to_7_segment_decoder_1: pin names not known; wires that end beside it: bcd_to_7_segment_decoder_1_p1, bcd_to_7_segment_decoder_1_p2, bcd_to_7_segment_decoder_1_p3, bcd_to_7_segment_decoder_1_p4, binary_to_bcd_converter_1_p2, bcd_to_7_segment_decoder_1_p6, bcd_to_7_segment_decoder_1_p7, bcd_to_7_segment_decoder_1_p8
  and and_10 (and_10_out, d_ff_2_qn, out_1[1], out_1[0]);
  and and_11 (and_11_out, d_ff_1_qn, out_1[2], out_1[1]);
  D_Flip_Flop d_ff_4 (.D(or_4_out), .clk(clock_1_out), .Q(out_1[0]), .Qn(d_ff_4_qn));  // open: preset, reset
  _7_Segment_Display u_7_segment_display_1 (
    .g(bcd_to_7_segment_decoder_1_p1), .f(bcd_to_7_segment_decoder_1_p3), .a(bcd_to_7_segment_decoder_1_p6),
    .b(bcd_to_7_segment_decoder_1_p8), .e(bcd_to_7_segment_decoder_1_p2), .d(bcd_to_7_segment_decoder_1_p4),
    .c(bcd_to_7_segment_decoder_1_p7));  // open: dp
  and and_12 (and_12_out, out_1[2], out_1[3], d_ff_3_qn, out_1[0]);
  // BCD_to_7_Segment_decoder bcd_to_7_segment_decoder_2: pin names not known; wires that end beside it: bcd_to_7_segment_decoder_2_p1, bcd_to_7_segment_decoder_2_p2, bcd_to_7_segment_decoder_2_p3, bcd_to_7_segment_decoder_2_p4, binary_to_bcd_converter_1_p3, bcd_to_7_segment_decoder_2_p6, bcd_to_7_segment_decoder_2_p7, bcd_to_7_segment_decoder_2_p8
  _7_Segment_Display u_7_segment_display_2 (
    .g(bcd_to_7_segment_decoder_2_p1), .f(bcd_to_7_segment_decoder_2_p3), .a(bcd_to_7_segment_decoder_2_p6),
    .b(bcd_to_7_segment_decoder_2_p8), .e(bcd_to_7_segment_decoder_2_p2), .d(bcd_to_7_segment_decoder_2_p4),
    .c(bcd_to_7_segment_decoder_2_p7));  // open: dp
endmodule

module q4 (
  output [5:0] out_1
);

  wire and_1_out, clock_1_out, not_1_out, not_2_out;

  Clock clock_1 (.out(clock_1_out));
  Counter #(.max('h3f), .width(6)) counter_1 (
    .clr(and_1_out), .load(1'b0), .up(1'b1), .clk(clock_1_out), .Q(out_1));  // open: count, D, carry
  and and_1 (and_1_out, not_1_out, not_2_out, out_1[2], out_1[3], out_1[4], out_1[5]);
  not not_1 (not_1_out, out_1[0]);
  not not_2 (not_2_out, out_1[1]);
endmodule
