// Logisim project q4b.circ as structural Verilog: 4 circuits, main circuit main
module main (
  input  Alarm_Toggle
);

  wire and_2_out, clock_1_out, counter_1_carry, counter_2_carry, counter_3_carry, hours_carry,
       Increment_Hours_out, Increment_Minutes_out, Increment_seconds_out, minutes_carry, not_1_out,
       not_2_out, not_3_out, or_1_out, or_2_out, or_3_out, seconds_carry, Set_Load_Time_out;
  wire [5:0] and_1_out, counter_1_q, counter_2_q, counter_3_q, hours_q, minutes_q, seconds_q, xnor_1_out,
       xnor_2_out, xnor_3_out;
  wire [13:0] binaryto7seg_1_out_2, binaryto7seg_2_out_2, binaryto7seg_3_out_2, binaryto7seg_4_out_2,
       binaryto7seg_5_out_2, binaryto7seg_6_out_2;

  Clock clock_1 (.out(clock_1_out));
  _7_Segment_Display u_7_segment_display_1 (
    .g(binaryto7seg_1_out_2[6]), .f(binaryto7seg_1_out_2[5]), .a(binaryto7seg_1_out_2[0]),
    .b(binaryto7seg_1_out_2[1]), .e(binaryto7seg_1_out_2[4]), .d(binaryto7seg_1_out_2[3]),
    .c(binaryto7seg_1_out_2[2]));  // open: dp
  _7_Segment_Display u_7_segment_display_2 (
    .g(binaryto7seg_2_out_2[6]), .f(binaryto7seg_2_out_2[5]), .a(binaryto7seg_2_out_2[0]),
    .b(binaryto7seg_2_out_2[1]), .e(binaryto7seg_2_out_2[4]), .d(binaryto7seg_2_out_2[3]),
    .c(binaryto7seg_2_out_2[2]));  // open: dp
  Counter #(.width(6), .max('h18)) hours (
    .load(Set_Load_Time_out), .D(counter_1_q), .count(not_1_out), .Q(hours_q), .carry(hours_carry),
    .clk(or_1_out), .clr(hours_carry));
  not not_1 (not_1_out, Set_Load_Time_out);
  _7_Segment_Display u_7_segment_display_3 (
    .g(binaryto7seg_1_out_2[13]), .f(binaryto7seg_1_out_2[12]), .a(binaryto7seg_1_out_2[7]),
    .b(binaryto7seg_1_out_2[8]), .e(binaryto7seg_1_out_2[11]), .d(binaryto7seg_1_out_2[10]),
    .c(binaryto7seg_1_out_2[9]));  // open: dp
  Counter #(.width(6), .max('h18), .trigger("falling")) counter_1 (
    .load(1'b0), .count(1'b1), .Q(counter_1_q), .carry(counter_1_carry), .clk(Increment_Hours_out),
    .clr(counter_1_carry));  // open: D
  _7_Segment_Display u_7_segment_display_4 (
    .g(binaryto7seg_2_out_2[13]), .f(binaryto7seg_2_out_2[12]), .a(binaryto7seg_2_out_2[7]),
    .b(binaryto7seg_2_out_2[8]), .e(binaryto7seg_2_out_2[11]), .d(binaryto7seg_2_out_2[10]),
    .c(binaryto7seg_2_out_2[9]));  // open: dp
  or or_1 (or_1_out, Set_Load_Time_out, minutes_carry);
  binaryto7seg binaryto7seg_1 (.in_1(hours_q), .out_2(binaryto7seg_1_out_2));
  binaryto7seg binaryto7seg_2 (.in_1(counter_1_q), .out_2(binaryto7seg_2_out_2));
  _7_Segment_Display u_7_segment_display_5 (
    .g(binaryto7seg_3_out_2[6]), .f(binaryto7seg_3_out_2[5]), .a(binaryto7seg_3_out_2[0]),
    .b(binaryto7seg_3_out_2[1]), .e(binaryto7seg_3_out_2[4]), .d(binaryto7seg_3_out_2[3]),
    .c(binaryto7seg_3_out_2[2]));  // open: dp
  _7_Segment_Display u_7_segment_display_6 (
    .g(binaryto7seg_4_out_2[6]), .f(binaryto7seg_4_out_2[5]), .a(binaryto7seg_4_out_2[0]),
    .b(binaryto7seg_4_out_2[1]), .e(binaryto7seg_4_out_2[4]), .d(binaryto7seg_4_out_2[3]),
    .c(binaryto7seg_4_out_2[2]));  // open: dp
  Counter #(.width(6), .max('h3c)) minutes (
    .load(Set_Load_Time_out), .D(counter_2_q), .count(not_2_out), .Q(minutes_q), .carry(minutes_carry),
    .clk(or_2_out), .clr(minutes_carry));
  not not_2 (not_2_out, Set_Load_Time_out);
  _7_Segment_Display u_7_segment_display_7 (
    .g(binaryto7seg_3_out_2[13]), .f(binaryto7seg_3_out_2[12]), .a(binaryto7seg_3_out_2[7]),
    .b(binaryto7seg_3_out_2[8]), .e(binaryto7seg_3_out_2[11]), .d(binaryto7seg_3_out_2[10]),
    .c(binaryto7seg_3_out_2[9]));  // open: dp
  Counter #(.width(6), .max('h3c), .trigger("falling")) counter_2 (
    .load(1'b0), .count(1'b1), .Q(counter_2_q), .carry(counter_2_carry), .clk(Increment_Minutes_out),
    .clr(counter_2_carry));  // open: D
  _7_Segment_Display u_7_segment_display_8 (
    .g(binaryto7seg_4_out_2[13]), .f(binaryto7seg_4_out_2[12]), .a(binaryto7seg_4_out_2[7]),
    .b(binaryto7seg_4_out_2[8]), .e(binaryto7seg_4_out_2[11]), .d(binaryto7seg_4_out_2[10]),
    .c(binaryto7seg_4_out_2[9]));  // open: dp
  or or_2 (or_2_out, Set_Load_Time_out, seconds_carry);
  binaryto7seg binaryto7seg_3 (.in_1(minutes_q), .out_2(binaryto7seg_3_out_2));
  binaryto7seg binaryto7seg_4 (.in_1(counter_2_q), .out_2(binaryto7seg_4_out_2));
  or or_3 (or_3_out, Set_Load_Time_out, clock_1_out);
  not not_3 (not_3_out, Set_Load_Time_out);
  _7_Segment_Display u_7_segment_display_9 (
    .g(binaryto7seg_5_out_2[6]), .f(binaryto7seg_5_out_2[5]), .a(binaryto7seg_5_out_2[0]),
    .b(binaryto7seg_5_out_2[1]), .e(binaryto7seg_5_out_2[4]), .d(binaryto7seg_5_out_2[3]),
    .c(binaryto7seg_5_out_2[2]));  // open: dp
  Counter #(.width(6), .max('h3c), .trigger("falling")) counter_3 (
    .load(1'b0), .count(1'b1), .Q(counter_3_q), .carry(counter_3_carry), .clk(Increment_seconds_out),
    .clr(counter_3_carry));  // open: D
  _7_Segment_Display u_7_segment_display_10 (
    .g(binaryto7seg_6_out_2[6]), .f(binaryto7seg_6_out_2[5]), .a(binaryto7seg_6_out_2[0]),
    .b(binaryto7seg_6_out_2[1]), .e(binaryto7seg_6_out_2[4]), .d(binaryto7seg_6_out_2[3]),
    .c(binaryto7seg_6_out_2[2]));  // open: dp
  Counter #(.width(6), .max('h3c)) seconds (
    .load(Set_Load_Time_out), .D(counter_3_q), .count(not_3_out), .Q(seconds_q), .carry(seconds_carry),
    .clk(or_3_out), .clr(seconds_carry));
  binaryto7seg binaryto7seg_5 (.in_1(seconds_q), .out_2(binaryto7seg_5_out_2));
  _7_Segment_Display u_7_segment_display_11 (
    .g(binaryto7seg_5_out_2[13]), .f(binaryto7seg_5_out_2[12]), .a(binaryto7seg_5_out_2[7]),
    .b(binaryto7seg_5_out_2[8]), .e(binaryto7seg_5_out_2[11]), .d(binaryto7seg_5_out_2[10]),
    .c(binaryto7seg_5_out_2[9]));  // open: dp
  binaryto7seg binaryto7seg_6 (.in_1(counter_3_q), .out_2(binaryto7seg_6_out_2));
  _7_Segment_Display u_7_segment_display_12 (
    .g(binaryto7seg_6_out_2[13]), .f(binaryto7seg_6_out_2[12]), .a(binaryto7seg_6_out_2[7]),
    .b(binaryto7seg_6_out_2[8]), .e(binaryto7seg_6_out_2[11]), .d(binaryto7seg_6_out_2[10]),
    .c(binaryto7seg_6_out_2[9]));  // open: dp
  assign xnor_1_out = ~(seconds_q ^ counter_3_q);  // XNOR_Gate xnor_1, 6 bits wide
  Button Set_Load_Time (.out(Set_Load_Time_out));
  Button Increment_Hours (.out(Increment_Hours_out));
  Button Increment_Minutes (.out(Increment_Minutes_out));
  Button Increment_seconds (.out(Increment_seconds_out));
  assign xnor_2_out = ~(minutes_q ^ counter_2_q);  // XNOR_Gate xnor_2, 6 bits wide
  assign xnor_3_out = ~(hours_q ^ counter_1_q);  // XNOR_Gate xnor_3, 6 bits wide
  assign and_1_out = xnor_1_out & xnor_2_out & xnor_3_out;  // AND_Gate and_1, 6 bits wide
  and and_2 (and_2_out, Alarm_Toggle, and_1_out[5], and_1_out[4], and_1_out[3], and_1_out[2], and_1_out[1], and_1_out[0]);
  LED led_1 (.in(and_2_out));

  // Notes on the sheet:
  //   HRS
  //   Mins
  //   CLOCK 
  //   Counters for Time Setter / Load / Alarm
  //   Seconds
  //   Alarm
endmodule

module binarytobcd (
  input  a5,
  input  a4,
  input  a3,
  input  a2,
  input  a1,
  input  a0,
  output b6,
  output b5,
  output b4,
  output b3,
  output b2,
  output b1,
  output b0
);

  wire and_1_out, and_2_out, and_3_out, and_4_out, and_5_out, and_6_out, and_7_out, and_8_out, and_9_out,
       and_10_out, and_11_out, and_12_out, and_13_out, and_14_out, and_15_out, and_16_out, and_17_out,
       and_18_out, and_19_out, and_20_out, and_21_out, and_22_out, and_23_out, and_24_out, and_25_out,
       and_26_out, and_27_out, and_28_out, and_29_out, and_30_out, and_31_out, and_32_out, and_33_out,
       and_34_out, and_35_out, and_36_out, and_37_out, and_38_out, not_1_out, not_2_out, not_3_out,
       not_4_out, not_5_out, not_6_out, not_7_out, not_8_out, not_9_out, not_10_out, not_11_out, not_12_out,
       not_13_out, not_14_out, not_15_out, not_16_out, not_17_out, not_18_out, not_19_out, not_20_out,
       not_21_out, not_22_out, not_23_out, not_24_out, not_25_out, not_26_out, not_27_out, not_28_out,
       not_29_out, not_30_out, not_31_out, not_32_out, not_33_out, not_34_out, not_35_out, not_36_out,
       not_37_out, not_38_out, not_39_out, not_40_out, not_41_out, not_42_out, not_43_out, not_44_out,
       not_45_out, not_46_out, not_47_out, not_48_out, not_49_out, not_50_out, not_51_out, not_52_out,
       not_53_out, not_54_out, not_55_out, not_56_out, not_57_out, not_58_out, not_59_out, not_60_out,
       not_61_out, not_62_out, not_63_out, not_64_out, not_65_out, not_66_out, not_67_out, not_68_out,
       not_69_out, not_70_out, not_71_out;

  and and_1 (and_1_out, a5, a3);
  and and_2 (and_2_out, a5, a4);
  not not_1 (not_1_out, a5);
  not not_2 (not_2_out, a5);
  not not_3 (not_3_out, a4);
  not not_4 (not_4_out, a3);
  not not_5 (not_5_out, a5);
  not not_6 (not_6_out, a4);
  not not_7 (not_7_out, a5);
  not not_8 (not_8_out, a4);
  not not_9 (not_9_out, a5);
  not not_10 (not_10_out, a5);
  not not_11 (not_11_out, a3);
  not not_12 (not_12_out, a2);
  not not_13 (not_13_out, a4);
  not not_14 (not_14_out, a3);
  not not_15 (not_15_out, a3);
  not not_16 (not_16_out, a3);
  not not_17 (not_17_out, a2);
  not not_18 (not_18_out, a5);
  not not_19 (not_19_out, a4);
  not not_20 (not_20_out, a2);
  not not_21 (not_21_out, a1);
  not not_22 (not_22_out, a5);
  not not_23 (not_23_out, a3);
  not not_24 (not_24_out, a2);
  not not_25 (not_25_out, a5);
  not not_26 (not_26_out, a1);
  not not_27 (not_27_out, a4);
  not not_28 (not_28_out, a3);
  not not_29 (not_29_out, a3);
  not not_30 (not_30_out, a2);
  not not_31 (not_31_out, a1);
  not not_32 (not_32_out, a2);
  not not_33 (not_33_out, a4);
  not not_34 (not_34_out, a3);
  not not_35 (not_35_out, a1);
  not not_36 (not_36_out, a5);
  not not_37 (not_37_out, a4);
  not not_38 (not_38_out, a5);
  not not_39 (not_39_out, a2);
  not not_40 (not_40_out, a1);
  not not_41 (not_41_out, a5);
  not not_42 (not_42_out, a2);
  not not_43 (not_43_out, a2);
  not not_44 (not_44_out, a1);
  not not_45 (not_45_out, a4);
  not not_46 (not_46_out, a3);
  not not_47 (not_47_out, a2);
  not not_48 (not_48_out, a4);
  not not_49 (not_49_out, a3);
  not not_50 (not_50_out, a5);
  not not_51 (not_51_out, a4);
  not not_52 (not_52_out, a3);
  not not_53 (not_53_out, a5);
  not not_54 (not_54_out, a3);
  not not_55 (not_55_out, a5);
  not not_56 (not_56_out, a4);
  not not_57 (not_57_out, a1);
  not not_58 (not_58_out, a5);
  not not_59 (not_59_out, a3);
  not not_60 (not_60_out, a2);
  not not_61 (not_61_out, a1);
  not not_62 (not_62_out, a5);
  not not_63 (not_63_out, a2);
  not not_64 (not_64_out, a4);
  not not_65 (not_65_out, a3);
  not not_66 (not_66_out, a1);
  not not_67 (not_67_out, a3);
  not not_68 (not_68_out, a1);
  not not_69 (not_69_out, a4);
  not not_70 (not_70_out, a2);
  not not_71 (not_71_out, a1);
  or or_1 (b6, and_1_out, and_2_out);
  and and_3 (and_3_out, not_1_out, a4, a2);
  and and_4 (and_4_out, not_2_out, a4, a3);
  and and_5 (and_5_out, a4, a3, a2);
  and and_6 (and_6_out, a5, not_3_out, not_4_out);
  and and_7 (and_7_out, not_5_out, not_6_out, a3, a1);
  and and_8 (and_8_out, not_7_out, not_8_out, a3, a2);
  and and_9 (and_9_out, not_9_out, a3, a2, a1);
  and and_10 (and_10_out, not_10_out, a4, not_11_out, not_12_out);
  and and_11 (and_11_out, a5, not_13_out, not_14_out);
  and and_12 (and_12_out, a5, not_15_out, a1);
  and and_13 (and_13_out, a5, not_16_out, a2);
  and and_14 (and_14_out, a5, a4, a3, not_17_out);
  and and_15 (and_15_out, not_18_out, not_19_out, a3, not_20_out, not_21_out);
  and and_16 (and_16_out, not_22_out, a4, not_23_out, not_24_out, a1);
  and and_17 (and_17_out, not_25_out, a4, a3, a2, not_26_out);
  and and_18 (and_18_out, a5, not_27_out, not_28_out, a2, a1);
  and and_19 (and_19_out, a5, a4, not_29_out, not_30_out, not_31_out);
  and and_20 (and_20_out, a5, a4, a3, not_32_out, a1);
  and and_21 (and_21_out, not_33_out, not_34_out, a2, not_35_out);
  and and_22 (and_22_out, not_36_out, not_37_out, a2, a1);
  and and_23 (and_23_out, not_38_out, a4, not_39_out, not_40_out);
  and and_24 (and_24_out, not_41_out, a4, a3, not_42_out);
  and and_25 (and_25_out, a4, a3, not_43_out, not_44_out);
  and and_26 (and_26_out, a5, not_45_out, not_46_out, not_47_out, a1);
  and and_27 (and_27_out, a5, not_48_out, a3, a2);
  and and_28 (and_28_out, a5, a4, not_49_out, a2, a1);
  and and_29 (and_29_out, not_50_out, not_51_out, not_52_out, a1);
  and and_30 (and_30_out, not_53_out, not_54_out, a2, a1);
  and and_31 (and_31_out, not_55_out, not_56_out, a3, a2, not_57_out);
  and and_32 (and_32_out, not_58_out, a4, not_59_out, not_60_out, not_61_out);
  and and_33 (and_33_out, not_62_out, a4, a3, not_63_out, a1);
  and and_34 (and_34_out, a5, not_64_out, not_65_out, not_66_out);
  and and_35 (and_35_out, a5, not_67_out, a2, not_68_out);
  and and_36 (and_36_out, a5, not_69_out, a3, a1);
  and and_37 (and_37_out, a5, a3, a2, a1);
  and and_38 (and_38_out, a5, a4, a3, not_70_out, not_71_out);
  or or_2 (b5, and_3_out, and_4_out, and_5_out, and_6_out);
  or or_3 (b4, and_7_out, and_8_out, and_9_out, and_10_out, and_11_out, and_12_out, and_13_out, and_14_out);
  or or_4 (b3, and_15_out, and_16_out, and_17_out, and_18_out, and_19_out, and_20_out);
  or or_5 (b2, and_21_out, and_22_out, and_23_out, and_24_out, and_25_out, and_26_out, and_27_out, and_28_out);
  or or_6 (b1, and_29_out, and_30_out, and_31_out, and_32_out, and_33_out, and_34_out, and_35_out, and_36_out, and_37_out, and_38_out);

  assign b0 = a0;
endmodule

module bcdto7seg (
  input  s0,
  input  s1,
  input  s2,
  input  s3,
  output a,
  output b,
  output c,
  output d,
  output e,
  output f,
  output g
);

  wire and_1_out, and_2_out, and_3_out, and_4_out, and_5_out, and_6_out, and_7_out, and_8_out, and_9_out,
       and_10_out, and_11_out, and_12_out, and_13_out, and_14_out, and_15_out, and_16_out, not_1_out,
       not_2_out, not_3_out, not_4_out, not_5_out, not_6_out, not_7_out, not_8_out, not_9_out, not_10_out,
       not_11_out, not_12_out, not_13_out, not_14_out, not_15_out, not_16_out, not_17_out, not_18_out,
       not_19_out, not_20_out, not_21_out;

  not not_1 (not_1_out, s2);
  and and_1 (and_1_out, not_1_out, not_2_out);
  not not_2 (not_2_out, s0);
  and and_2 (and_2_out, s2, s0);
  not not_3 (not_3_out, s2);
  not not_4 (not_4_out, s1);
  and and_3 (and_3_out, not_4_out, not_5_out);
  not not_5 (not_5_out, s0);
  and and_4 (and_4_out, s1, s0);
  not not_6 (not_6_out, s1);
  or or_1 (c, not_6_out, s0, s2);
  not not_7 (not_7_out, s2);
  and and_5 (and_5_out, not_7_out, not_8_out);
  not not_8 (not_8_out, s0);
  not not_9 (not_9_out, s2);
  and and_6 (and_6_out, not_9_out, s1);
  and and_7 (and_7_out, s1, not_10_out);
  not not_10 (not_10_out, s0);
  and and_8 (and_8_out, s2, not_11_out, s0);
  not not_11 (not_11_out, s1);
  not not_12 (not_12_out, s2);
  and and_9 (and_9_out, not_12_out, not_13_out);
  not not_13 (not_13_out, s0);
  and and_10 (and_10_out, s1, not_14_out);
  not not_14 (not_14_out, s0);
  not not_15 (not_15_out, s1);
  and and_11 (and_11_out, not_15_out, not_16_out);
  not not_16 (not_16_out, s0);
  and and_12 (and_12_out, s2, not_17_out);
  not not_17 (not_17_out, s1);
  and and_13 (and_13_out, s2, not_18_out);
  not not_18 (not_18_out, s0);
  not not_19 (not_19_out, s2);
  and and_14 (and_14_out, not_19_out, s1);
  and and_15 (and_15_out, s2, not_20_out);
  not not_20 (not_20_out, s1);
  and and_16 (and_16_out, s2, not_21_out);
  not not_21 (not_21_out, s0);
  or or_2 (a, and_1_out, s1, and_2_out, s3);
  or or_3 (b, not_3_out, and_3_out, and_4_out);
  or or_4 (d, and_5_out, and_6_out, and_7_out, and_8_out, s3);
  or or_5 (e, and_9_out, and_10_out);
  or or_6 (f, and_11_out, and_12_out, and_13_out, s3);
  or or_7 (g, and_14_out, and_15_out, and_16_out, s3);
endmodule

module binaryto7seg (
  input  [5:0] in_1,
  output [13:0] out_2
);

  wire binarytobcd_1_b0, binarytobcd_1_b1, binarytobcd_1_b2, binarytobcd_1_b3, binarytobcd_1_b4,
       binarytobcd_1_b5, binarytobcd_1_b6;

  binarytobcd binarytobcd_1 (
    .a5(in_1[5]), .a4(in_1[4]), .a3(in_1[3]), .a2(in_1[2]), .a1(in_1[1]), .a0(in_1[0]),
    .b6(binarytobcd_1_b6), .b5(binarytobcd_1_b5), .b4(binarytobcd_1_b4), .b3(binarytobcd_1_b3),
    .b2(binarytobcd_1_b2), .b1(binarytobcd_1_b1), .b0(binarytobcd_1_b0));
  bcdto7seg bcdto7seg_1 (
    .s0(binarytobcd_1_b4), .s1(binarytobcd_1_b5), .s2(binarytobcd_1_b6), .s3(1'b0), .a(out_2[0]),
    .b(out_2[1]), .c(out_2[2]), .d(out_2[3]), .e(out_2[4]), .f(out_2[5]), .g(out_2[6]));
  bcdto7seg bcdto7seg_2 (
    .s0(binarytobcd_1_b0), .s1(binarytobcd_1_b1), .s2(binarytobcd_1_b2), .s3(binarytobcd_1_b3), .a(out_2[7]),
    .b(out_2[8]), .c(out_2[9]), .d(out_2[10]), .e(out_2[11]), .f(out_2[12]), .g(out_2[13]));
endmodule
