// Logisim project lol.circ as structural Verilog: 1 circuit, main circuit main
module main (
  input  C
);

  wire and_1_out, and_2_out, and_3_out, and_4_out, and_5_out, and_6_out, and_7_out, and_8_out, and_9_out,
       clock_1_out, d_ff_1_q, d_ff_1_qn, d_ff_3_q, d_ff_3_qn, d_ff_4_q, d_ff_4_qn, d_ff_6_q, d_ff_7_q,
       d_ff_7_qn, decoder_1_out0, decoder_1_out1, decoder_1_out2, decoder_1_out3, not_1_out, not_2_out,
       not_3_out, not_4_out, or_1_out, or_2_out, or_3_out, or_4_out, or_5_out, or_6_out, or_7_out, ST_out,
       xor_1_out, xor_2_out;
  wire [1:0] d_ff_5_q;

  Clock clock_1 (.out(clock_1_out));
  or or_1 (or_1_out, and_2_out, and_1_out);
  and and_1 (and_1_out, d_ff_4_q, d_ff_3_q, d_ff_1_qn);
  not not_1 (not_1_out, ST_out);
  not not_2 (not_2_out, and_9_out);
  or or_2 (or_2_out, and_9_out, not_3_out);
  not not_3 (not_3_out, C);
  not not_4 (not_4_out, ST_out);
  Decoder #(.select(2)) decoder_1 (
    .out0(decoder_1_out0), .out1(decoder_1_out1), .out2(decoder_1_out2), .out3(decoder_1_out3), .sel(d_ff_5_q));  // open: en
  and and_2 (and_2_out, or_3_out, d_ff_1_q);
  D_Flip_Flop #(.trigger("falling")) d_ff_1 (
    .D(or_1_out), .clk(clock_1_out), .Q(d_ff_1_q), .Qn(d_ff_1_qn));  // open: preset, reset
  and and_3 (and_3_out, C, and_9_out, decoder_1_out0);
  and and_4 (and_4_out, decoder_1_out1, ST_out);
  and and_5 (and_5_out, not_1_out, decoder_1_out1);
  and and_6 (and_6_out, decoder_1_out2, C, not_2_out);
  and and_7 (and_7_out, decoder_1_out2, or_2_out);
  and and_8 (and_8_out, decoder_1_out3, not_4_out);
  D_Flip_Flop d_ff_2 (.D(or_5_out), .clk(clock_1_out), .Q(d_ff_5_q[1]));  // open: Qn, preset, reset
  or or_3 (or_3_out, d_ff_4_qn, d_ff_3_qn);
  xor xor_1 (xor_1_out, d_ff_4_q, d_ff_3_q);
  D_Flip_Flop #(.trigger("falling")) d_ff_3 (
    .D(xor_1_out), .clk(clock_1_out), .Q(d_ff_3_q), .Qn(d_ff_3_qn));  // open: preset, reset
  or or_4 (or_4_out, and_3_out, and_5_out, and_7_out, and_8_out);
  or or_5 (or_5_out, and_4_out, and_6_out, and_7_out, and_8_out);
  and and_9 (and_9_out, d_ff_1_q, d_ff_3_q, d_ff_4_q);
  D_Flip_Flop #(.trigger("falling")) d_ff_4 (
    .D(d_ff_4_qn), .clk(clock_1_out), .Q(d_ff_4_q), .Qn(d_ff_4_qn));  // open: preset, reset
  D_Flip_Flop d_ff_5 (.D(or_4_out), .clk(clock_1_out), .Q(d_ff_5_q[0]));  // open: Qn, preset, reset
  xor xor_2 (xor_2_out, d_ff_7_q, d_ff_6_q);
  D_Flip_Flop d_ff_6 (.D(xor_2_out), .clk(clock_1_out), .Q(d_ff_6_q), .reset(and_9_out));  // open: Qn, preset
  and ST (ST_out, d_ff_7_q, d_ff_6_q);
  D_Flip_Flop d_ff_7 (
    .D(d_ff_7_qn), .clk(clock_1_out), .Q(d_ff_7_q), .Qn(d_ff_7_qn), .reset(and_9_out));  // open: preset
  or or_6 (or_6_out, decoder_1_out3, decoder_1_out2);
  LED Highway_red (.in(or_6_out));
  LED Highway_yellow (.in(decoder_1_out1));
  LED Highway_green (.in(decoder_1_out0));
  or or_7 (or_7_out, decoder_1_out1, decoder_1_out0);
  LED NITK_red (.in(or_7_out));
  LED NITK_yellow (.in(decoder_1_out3));
  LED NITK_green (.in(decoder_1_out2));

  // Notes on the sheet:
  //   for tlf and tlh
  //   Long timer(8 clocks)
  //   Short Timer (4 clocks)
endmodule
