// Logisim project q1.circ as structural Verilog: 2 circuits, main circuit main
module main (
  input  in_1,
  output out_2
);

  wire and_1_out, and_2_out, and_3_out, and_4_out, and_5_out, clock_1_out, d_ff_1_q, d_ff_1_qn, d_ff_2_q,
       d_ff_2_qn, not_1_out, or_1_out, or_2_out;

  Clock clock_1 (.out(clock_1_out));
  or or_1 (or_1_out, and_1_out, and_2_out);
  and and_1 (and_1_out, in_1, d_ff_2_q, d_ff_1_qn);
  and and_2 (and_2_out, d_ff_2_qn, d_ff_1_q);
  D_Flip_Flop d_ff_1 (.D(or_1_out), .clk(clock_1_out), .Q(d_ff_1_q), .Qn(d_ff_1_qn));  // open: preset, reset
  and and_3 (and_3_out, in_1, d_ff_2_qn, d_ff_1_qn);
  not not_1 (not_1_out, in_1);
  and and_4 (and_4_out, d_ff_2_q, d_ff_1_q, in_1);
  and and_5 (and_5_out, d_ff_1_q, d_ff_2_qn, not_1_out);
  or or_2 (or_2_out, and_3_out, and_4_out, and_5_out);
  D_Flip_Flop d_ff_2 (.D(or_2_out), .clk(clock_1_out), .Q(d_ff_2_q), .Qn(d_ff_2_qn));  // open: preset, reset
  and and_6 (out_2, in_1, d_ff_2_q, d_ff_1_q);
endmodule

module jkq1 (
  input  X,
  output Y
);

  wire and_1_out, and_2_out, and_3_out, clk_out, j_k_ff_1_q, j_k_ff_1_qn, j_k_ff_2_q, not_1_out, or_1_out,
       or_2_out, or_3_out;

  Clock clk (.out(clk_out));
  or or_1 (or_1_out, X, j_k_ff_1_q);
  and and_1 (and_1_out, or_1_out, j_k_ff_2_q);
  J_K_Flip_Flop j_k_ff_1 (
    .J(and_1_out), .K(and_1_out), .clk(clk_out), .Q(j_k_ff_1_q), .Qn(j_k_ff_1_qn));  // open: preset, reset
  or or_2 (or_2_out, j_k_ff_2_q, X);
  not not_1 (not_1_out, X);
  and and_2 (and_2_out, not_1_out, j_k_ff_1_q);
  and and_3 (and_3_out, or_2_out, j_k_ff_1_qn);
  J_K_Flip_Flop j_k_ff_2 (.J(or_3_out), .K(or_3_out), .clk(clk_out), .Q(j_k_ff_2_q));  // open: Qn, preset, reset
  or or_3 (or_3_out, and_2_out, and_3_out);
  and and_4 (Y, X, j_k_ff_2_q, j_k_ff_1_q);
endmodule
